// Logisim project hw02.circ as structural Verilog: 2 circuits, main circuit main
module main (
);

  wire and_2_out, not_1_out, not_2_out, or_1_out, or_2_out, undriven, undriven_2, undriven_3, undriven_4,
       undriven_5, undriven_6, undriven_7, undriven_8, undriven_9;

  // AND_Gate and_1 is placed but not wired
  not not_1 (not_1_out, undriven);
  not not_2 (not_2_out, undriven_2);
  and and_2 (and_2_out, not_1_out, not_2_out);
  or or_1 (or_1_out, and_2_out, undriven_2);
  or or_2 (or_2_out, undriven_3, undriven_4, undriven_5, undriven_6);
  // OR_Gate or_3 has open pins: in1=undriven_7, in2=undriven_8, in3=undriven_9, out=open
  Transistor #(.\type ("n")) transistor_1 ();  // open: in, out, gate

  // Notes on the sheet:
  //   in1
  //   in0
  //   A
  //   B
  //   C
  //   D
  //   f(in0,in1)
  //   Z
endmodule

module _11 (
);

  wire adder_1_cout, adder_2_cout, adder_3_cout, and_1_out, and_2_out, and_3_out, and_4_out, not_1_out,
       not_2_out, not_3_out, not_4_out, not_5_out, not_6_out, or_1_out, transistor_1_out, transistor_2_out,
       transistor_5_out, transistor_6_out, undriven, undriven_2, undriven_3, undriven_4, undriven_6,
       undriven_8, undriven_10, undriven_12;
  wire [1:0] undriven_13;
  wire [7:0] adder_1_out, adder_2_out, adder_3_out, adder_4_out, multiplexer_1_out, multiplexer_2_out,
       multiplexer_3_out, multiplexer_4_out, undriven_5, undriven_7, undriven_9, undriven_11;

  Transistor transistor_1 (.in(transistor_2_out), .out(transistor_1_out), .gate(undriven_2));
  Transistor #(.\type ("n")) transistor_2 (.in(1'b0), .out(transistor_2_out), .gate(undriven_2));
  not not_1 (not_1_out, undriven_4);
  Transistor transistor_3 (.in(transistor_5_out), .out(transistor_1_out), .gate(transistor_2_out));
  not not_2 (not_2_out, undriven_3);
  Transistor transistor_4 (.in(transistor_5_out), .out(transistor_1_out), .gate(undriven));
  Transistor #(.\type ("n")) transistor_5 (.in(transistor_6_out), .out(transistor_5_out), .gate(transistor_2_out));
  Transistor #(.\type ("n")) transistor_6 (.in(1'b0), .out(transistor_6_out), .gate(undriven));
  and and_1 (and_1_out, undriven_4, undriven_3);
  and and_2 (and_2_out, not_1_out, not_2_out);
  and and_3 (and_3_out, not_2_out, undriven_4);
  and and_4 (and_4_out, not_1_out, undriven_3);
  or or_1 (or_1_out, and_1_out, and_2_out);
  Multiplexer #(.select(2), .enable("false")) multiplexer_1 (
    .in0(undriven_6), .in3(not_3_out), .out(multiplexer_1_out[0]), .sel(undriven_13));  // open: in1, in2
  not not_3 (not_3_out, undriven_6);
  Multiplexer #(.select(2), .enable("false")) multiplexer_2 (
    .in0(undriven_8), .in3(not_4_out), .out(multiplexer_2_out[0]), .sel(undriven_13));  // open: in1, in2
  not not_4 (not_4_out, undriven_8);
  Multiplexer #(.select(2), .enable("false")) multiplexer_3 (
    .in0(undriven_10), .in3(not_5_out), .out(multiplexer_3_out[0]), .sel(undriven_13));  // open: in1, in2
  not not_5 (not_5_out, undriven_10);
  Multiplexer #(.select(2), .enable("false")) multiplexer_4 (
    .in0(undriven_12), .in3(not_6_out), .out(multiplexer_4_out[0]), .sel(undriven_13));  // open: in1, in2
  not not_6 (not_6_out, undriven_12);
  Adder adder_1 (.a(undriven_5), .b(multiplexer_1_out), .out(adder_1_out), .cin(undriven_13[0]), .cout(adder_1_cout));
  Adder adder_2 (.a(undriven_7), .b(multiplexer_2_out), .out(adder_2_out), .cin(adder_1_cout), .cout(adder_2_cout));
  Adder adder_3 (.a(undriven_9), .b(multiplexer_3_out), .out(adder_3_out), .cin(adder_2_cout), .cout(adder_3_cout));
  Adder adder_4 (.a(undriven_11), .b(multiplexer_4_out), .out(adder_4_out), .cin(adder_3_cout));  // open: cout
  // Pins of 1 and 8 bits meet at multiplexer_4_out
  // Pins of 1 and 2 bits meet at undriven_13
  // Pins of 1 and 8 bits meet at multiplexer_1_out
  // Pins of 1 and 8 bits meet at multiplexer_2_out
  // Pins of 1 and 8 bits meet at multiplexer_3_out
  // also tied to VCC on the sheet: transistor_1_out

  // Notes on the sheet:
  //   in0
  //   in1
  //   A
  //   B
  //   f(in0,in1)
  //   L
  //   G
  //   E
  //   A0
  //   B0
  //   A1
  //   B1
  //   A2
  //   B2
  //   A3
  //   B3
  //   X
  //   S0
  //   S1
  //   S2
  //   S3
endmodule
